// Logisim project DMux4Way.circ as structural Verilog: 1 circuit, main circuit main
module main (
  input  in_1,
  input  [1:0] in_2,
  output out_3,
  output out_4,
  output out_5,
  output out_6
);

  wire demultiplexer_2_out0, demultiplexer_2_out1;

  Demultiplexer #(.enable("false")) demultiplexer_1 (
    .out0(out_3), .out1(out_4), .in(demultiplexer_2_out0), .sel(in_2[0]));
  Demultiplexer #(.enable("false")) demultiplexer_2 (
    .out0(demultiplexer_2_out0), .out1(demultiplexer_2_out1), .in(in_1), .sel(in_2[1]));
  Demultiplexer #(.enable("false")) demultiplexer_3 (
    .out0(out_5), .out1(out_6), .in(demultiplexer_2_out1), .sel(in_2[0]));
endmodule
