// Logisim project Mux16.circ as structural Verilog: 1 circuit, main circuit main
module main (
  input  in_1,
  input  [15:0] in_2,
  input  [15:0] in_3,
  output [15:0] out_4
);

  Multiplexer #(.enable("false")) multiplexer_1 (.in0(in_2[0]), .in1(in_3[0]), .out(out_4[0]), .sel(in_1));
  Multiplexer #(.enable("false")) multiplexer_2 (.in0(in_2[1]), .in1(in_3[1]), .out(out_4[1]), .sel(in_1));
  Multiplexer #(.enable("false")) multiplexer_3 (.in0(in_2[2]), .in1(in_3[2]), .out(out_4[2]), .sel(in_1));
  Multiplexer #(.enable("false")) multiplexer_4 (.in0(in_2[3]), .in1(in_3[3]), .out(out_4[3]), .sel(in_1));
  Multiplexer #(.enable("false")) multiplexer_5 (.in0(in_2[4]), .in1(in_3[4]), .out(out_4[4]), .sel(in_1));
  Multiplexer #(.enable("false")) multiplexer_6 (.in0(in_2[5]), .in1(in_3[5]), .out(out_4[5]), .sel(in_1));
  Multiplexer #(.enable("false")) multiplexer_7 (.in0(in_2[6]), .in1(in_3[6]), .out(out_4[6]), .sel(in_1));
  Multiplexer #(.enable("false")) multiplexer_8 (.in0(in_2[7]), .in1(in_3[7]), .out(out_4[7]), .sel(in_1));
  Multiplexer #(.enable("false")) multiplexer_9 (.in0(in_2[8]), .in1(in_3[8]), .out(out_4[8]), .sel(in_1));
  Multiplexer #(.enable("false")) multiplexer_10 (.in0(in_2[9]), .in1(in_3[9]), .out(out_4[9]), .sel(in_1));
  Multiplexer #(.enable("false")) multiplexer_11 (.in0(in_2[10]), .in1(in_3[10]), .out(out_4[10]), .sel(in_1));
  Multiplexer #(.enable("false")) multiplexer_12 (.in0(in_2[11]), .in1(in_3[11]), .out(out_4[11]), .sel(in_1));
  Multiplexer #(.enable("false")) multiplexer_13 (.in0(in_2[12]), .in1(in_3[12]), .out(out_4[12]), .sel(in_1));
  Multiplexer #(.enable("false")) multiplexer_14 (.in0(in_2[13]), .in1(in_3[13]), .out(out_4[13]), .sel(in_1));
  Multiplexer #(.enable("false")) multiplexer_15 (.in0(in_2[14]), .in1(in_3[14]), .out(out_4[14]), .sel(in_1));
  Multiplexer #(.enable("false")) multiplexer_16 (.in0(in_2[15]), .in1(in_3[15]), .out(out_4[15]), .sel(in_1));
endmodule
