// Logisim project Or16.circ as structural Verilog: 1 circuit, main circuit main
module main (
  input  [15:0] in_1,
  input  [15:0] in_2,
  output [15:0] out_3
);

  or or_1 (out_3[0], in_1[0], in_2[0]);
  or or_2 (out_3[1], in_1[1], in_2[1]);
  or or_3 (out_3[2], in_1[2], in_2[2]);
  or or_4 (out_3[3], in_1[3], in_2[3]);
  or or_5 (out_3[4], in_1[4], in_2[4]);
  or or_6 (out_3[5], in_1[5], in_2[5]);
  or or_7 (out_3[6], in_1[6], in_2[6]);
  or or_8 (out_3[8], in_1[8], in_2[8]);
  or or_9 (out_3[7], in_1[7], in_2[7]);
  or or_10 (out_3[9], in_1[9], in_2[9]);
  or or_11 (out_3[10], in_1[10], in_2[10]);
  or or_12 (out_3[12], in_1[12], in_2[12]);
  or or_13 (out_3[11], in_1[11], in_2[11]);
  or or_14 (out_3[13], in_1[13], in_2[13]);
  or or_15 (out_3[14], in_1[14], in_2[14]);
  or or_16 (out_3[15], in_1[15], in_2[15]);
endmodule
