// Logisim project Xor.circ as structural Verilog: 1 circuit, main circuit main
module main (
  input  in_1,
  input  in_2,
  input  in_3,
  input  in_4,
  output out_5,
  output out_6
);

  wire and_1_out, and_2_out, nand_1_out, not_1_out, not_2_out, or_2_out;

  not not_1 (not_1_out, in_3);
  not not_2 (not_2_out, in_1);
  and and_1 (and_1_out, in_1, not_1_out);
  and and_2 (and_2_out, not_2_out, in_3);
  or or_1 (out_6, and_1_out, and_2_out);
  or or_2 (or_2_out, in_2, in_4);
  and and_3 (out_5, or_2_out, nand_1_out);
  nand nand_1 (nand_1_out, in_4, in_2);
endmodule
