// Logisim project Add16.circ as structural Verilog: 1 circuit, main circuit main
module main (
  input  [15:0] in_1,
  input  [15:0] in_2,
  output [15:0] out_3
);

  wire FullAdder_2_carry, FullAdder_3_carry, FullAdder_4_carry, FullAdder_5_carry, FullAdder_6_carry,
       FullAdder_7_carry, FullAdder_8_carry, FullAdder_9_carry, FullAdder_10_carry, FullAdder_11_carry,
       FullAdder_12_carry, FullAdder_13_carry, FullAdder_15_carry, FullAdder_carry, HalfAdder_carry;

  HalfAdder HalfAdder (.in_1(in_1[0]), .in_2(in_2[0]), .Carry(HalfAdder_carry), .Sum(out_3[0]));
  FullAdder FullAdder (.in_1(HalfAdder_carry), .in_2(in_1[1]), .in_3(in_2[1]), .Carry(FullAdder_carry), .Sum(out_3[1]));
  FullAdder FullAdder_2 (
    .in_1(FullAdder_3_carry), .in_2(in_1[3]), .in_3(in_2[3]), .Carry(FullAdder_2_carry), .Sum(out_3[3]));
  FullAdder FullAdder_3 (
    .in_1(FullAdder_carry), .in_2(in_1[2]), .in_3(in_2[2]), .Carry(FullAdder_3_carry), .Sum(out_3[2]));
  FullAdder FullAdder_4 (
    .in_1(FullAdder_2_carry), .in_2(in_1[4]), .in_3(in_2[4]), .Carry(FullAdder_4_carry), .Sum(out_3[4]));
  FullAdder FullAdder_5 (
    .in_1(FullAdder_4_carry), .in_2(in_1[5]), .in_3(in_2[5]), .Carry(FullAdder_5_carry), .Sum(out_3[5]));
  FullAdder FullAdder_6 (
    .in_1(FullAdder_7_carry), .in_2(in_1[7]), .in_3(in_2[7]), .Carry(FullAdder_6_carry), .Sum(out_3[7]));
  FullAdder FullAdder_7 (
    .in_1(FullAdder_5_carry), .in_2(in_1[6]), .in_3(in_2[6]), .Carry(FullAdder_7_carry), .Sum(out_3[6]));
  FullAdder FullAdder_8 (
    .in_1(FullAdder_6_carry), .in_2(in_1[8]), .in_3(in_2[8]), .Carry(FullAdder_8_carry), .Sum(out_3[8]));
  FullAdder FullAdder_9 (
    .in_1(FullAdder_8_carry), .in_2(in_1[9]), .in_3(in_2[9]), .Carry(FullAdder_9_carry), .Sum(out_3[9]));
  FullAdder FullAdder_10 (
    .in_1(FullAdder_9_carry), .in_2(in_1[10]), .in_3(in_2[10]), .Carry(FullAdder_10_carry), .Sum(out_3[10]));
  FullAdder FullAdder_11 (
    .in_1(FullAdder_10_carry), .in_2(in_1[11]), .in_3(in_2[11]), .Carry(FullAdder_11_carry), .Sum(out_3[11]));
  FullAdder FullAdder_12 (
    .in_1(FullAdder_11_carry), .in_2(in_1[12]), .in_3(in_2[12]), .Carry(FullAdder_12_carry), .Sum(out_3[12]));
  FullAdder FullAdder_13 (
    .in_1(FullAdder_12_carry), .in_2(in_1[13]), .in_3(in_2[13]), .Carry(FullAdder_13_carry), .Sum(out_3[13]));
  FullAdder FullAdder_14 (.in_1(FullAdder_15_carry), .in_2(in_1[15]), .in_3(in_2[15]), .Sum(out_3[15]));  // open: Carry
  FullAdder FullAdder_15 (
    .in_1(FullAdder_13_carry), .in_2(in_1[14]), .in_3(in_2[14]), .Carry(FullAdder_15_carry), .Sum(out_3[14]));
endmodule
