// Logisim project FullAdder.circ as structural Verilog: 1 circuit, main circuit FullAdder
module FullAdder (
  input  in_1,
  input  in_2,
  input  in_3,
  output Carry,
  output Sum
);

  wire HalfAdder_2_carry, HalfAdder_carry, HalfAdder_sum;

  HalfAdder HalfAdder (.in_1(in_1), .in_2(in_2), .Carry(HalfAdder_carry), .Sum(HalfAdder_sum));
  or or_1 (Carry, HalfAdder_carry, HalfAdder_2_carry);
  HalfAdder HalfAdder_2 (.in_1(HalfAdder_sum), .in_2(in_3), .Carry(HalfAdder_2_carry), .Sum(Sum));
endmodule
