// Logisim project HalfAdder.circ as structural Verilog: 1 circuit, main circuit HalfAdder
module HalfAdder (
  input  in_1,
  input  in_2,
  output Carry,
  output Sum
);

  and and_1 (Carry, in_1, in_2);
  xor xor_1 (Sum, in_1, in_2);
endmodule
