// Logisim project Or16Way.circ as structural Verilog: 1 circuit, main circuit Or16Way
module Or16Way (
  input  [15:0] in_1,
  output out_2
);

  wire or_1_out, or_2_out;

  or or_1 (or_1_out, in_1[0], in_1[1], in_1[2], in_1[3], in_1[4], in_1[5], in_1[6], in_1[7]);
  or or_2 (or_2_out, in_1[8], in_1[9], in_1[10], in_1[11], in_1[12], in_1[13], in_1[14], in_1[15]);
  or or_3 (out_2, or_1_out, or_2_out);
endmodule
