// Logisim project Bit.circ as structural Verilog: 1 circuit, main circuit main
module main (
  input  Input,
  input  Load,
  output Output
);

  wire clock_1_out, multiplexer_1_out;

  Multiplexer #(.enable("false")) multiplexer_1 (.in0(Output), .in1(Input), .out(multiplexer_1_out), .sel(Load));
  D_Flip_Flop d_ff_1 (.clk(clock_1_out), .D(multiplexer_1_out), .Q(Output));  // open: Qn, preset, en, reset
  Clock clock_1 (.out(clock_1_out));

  // Notes on the sheet:
  //   1-bit Register ("Bit")
endmodule
