// Logisim project PC.circ as structural Verilog: 1 circuit, main circuit main
module main (
  input  [15:0] Input,
  input  inc,
  input  load,
  input  reset,
  output [15:0] Output
);

  wire clock_1_out;
  wire [15:0] main_1_out_2, multiplexer_1_out, multiplexer_2_out, multiplexer_3_out;

  Multiplexer #(.width(16), .enable("false")) multiplexer_1 (
    .in0(Output), .in1(main_1_out_2), .out(multiplexer_1_out), .sel(inc));
  Multiplexer #(.width(16), .enable("false")) multiplexer_2 (
    .in0(multiplexer_1_out), .in1(Input), .out(multiplexer_2_out), .sel(load));
  Multiplexer #(.width(16), .enable("false")) multiplexer_3 (
    .in0(multiplexer_2_out), .in1({16{1'b0}}), .out(multiplexer_3_out), .sel(reset));
  Clock clock_1 (.out(clock_1_out));
  Inc16_main main_1 (.in_1(Output), .out_2(main_1_out_2));
  Register #(.width(16)) register_1 (.D(multiplexer_3_out), .en(1'b1), .Q(Output), .clk(clock_1_out));  // open: clr

  // Notes on the sheet:
  //   PC (Program Counter)
endmodule
