// Logisim project RAM8.circ as structural Verilog: 1 circuit, main circuit main
module main (
  input  [15:0] Input,
  input  Load,
  input  [2:0] Address,
  output [15:0] Output
);

  wire clock_1_out, demultiplexer_1_out0, demultiplexer_1_out1, demultiplexer_1_out2, demultiplexer_1_out3,
       demultiplexer_1_out4, demultiplexer_1_out5, demultiplexer_1_out6, demultiplexer_1_out7;
  wire [15:0] register_1_q, register_2_q, register_3_q, register_4_q, register_5_q, register_6_q,
       register_7_q, register_8_q;

  Demultiplexer #(.select(3)) demultiplexer_1 (
    .out0(demultiplexer_1_out0), .out1(demultiplexer_1_out1), .out2(demultiplexer_1_out2),
    .out3(demultiplexer_1_out3), .out4(demultiplexer_1_out4), .out5(demultiplexer_1_out5),
    .out6(demultiplexer_1_out6), .out7(demultiplexer_1_out7), .in(Load), .sel(Address));  // open: en
  Register #(.width(16)) register_1 (
    .D(Input), .en(demultiplexer_1_out0), .Q(register_1_q), .clk(clock_1_out));  // open: clr
  Register #(.width(16)) register_2 (
    .D(Input), .en(demultiplexer_1_out2), .Q(register_2_q), .clk(clock_1_out));  // open: clr
  Register #(.width(16)) register_3 (
    .D(Input), .en(demultiplexer_1_out4), .Q(register_3_q), .clk(clock_1_out));  // open: clr
  Register #(.width(16)) register_4 (
    .D(Input), .en(demultiplexer_1_out6), .Q(register_4_q), .clk(clock_1_out));  // open: clr
  Clock clock_1 (.out(clock_1_out));
  Register #(.width(16)) register_5 (
    .D(Input), .en(demultiplexer_1_out1), .Q(register_5_q), .clk(clock_1_out));  // open: clr
  Register #(.width(16)) register_6 (
    .D(Input), .en(demultiplexer_1_out3), .Q(register_6_q), .clk(clock_1_out));  // open: clr
  Register #(.width(16)) register_7 (
    .D(Input), .en(demultiplexer_1_out5), .Q(register_7_q), .clk(clock_1_out));  // open: clr
  Register #(.width(16)) register_8 (
    .D(Input), .en(demultiplexer_1_out7), .Q(register_8_q), .clk(clock_1_out));  // open: clr
  Multiplexer #(.select(3), .width(16)) multiplexer_1 (
    .in0(register_1_q), .in1(register_5_q), .in2(register_2_q), .in3(register_6_q), .in4(register_3_q),
    .in5(register_7_q), .in6(register_4_q), .in7(register_8_q), .out(Output), .sel(Address));  // open: en

  // Notes on the sheet:
  //   RAM8
endmodule
