// Logisim project Register.circ as structural Verilog: 1 circuit, main circuit main
module main (
  input  in_1,
  input  [15:0] in_2,
  output [15:0] out_3
);

  wire clock_1_out;

  Clock clock_1 (.out(clock_1_out));
  Register #(.width(1)) register_1 (.D(in_2[0]), .en(in_1), .Q(out_3[0]), .clk(clock_1_out));  // open: clr
  Register #(.width(1)) register_2 (.D(in_2[1]), .en(in_1), .Q(out_3[1]), .clk(clock_1_out));  // open: clr
  Register #(.width(1)) register_3 (.D(in_2[2]), .en(in_1), .Q(out_3[2]), .clk(clock_1_out));  // open: clr
  Register #(.width(1)) register_4 (.D(in_2[3]), .en(in_1), .Q(out_3[3]), .clk(clock_1_out));  // open: clr
  Register #(.width(1)) register_5 (.D(in_2[4]), .en(in_1), .Q(out_3[4]), .clk(clock_1_out));  // open: clr
  Register #(.width(1)) register_6 (.D(in_2[5]), .en(in_1), .Q(out_3[5]), .clk(clock_1_out));  // open: clr
  Register #(.width(1)) register_7 (.D(in_2[6]), .en(in_1), .Q(out_3[6]), .clk(clock_1_out));  // open: clr
  Register #(.width(1)) register_8 (.D(in_2[7]), .en(in_1), .Q(out_3[7]), .clk(clock_1_out));  // open: clr
  Register #(.width(1)) register_9 (.D(in_2[8]), .en(in_1), .Q(out_3[8]), .clk(clock_1_out));  // open: clr
  Register #(.width(1)) register_10 (.D(in_2[9]), .en(in_1), .Q(out_3[9]), .clk(clock_1_out));  // open: clr
  Register #(.width(1)) register_11 (.D(in_2[10]), .en(in_1), .Q(out_3[10]), .clk(clock_1_out));  // open: clr
  Register #(.width(1)) register_12 (.D(in_2[11]), .en(in_1), .Q(out_3[11]), .clk(clock_1_out));  // open: clr
  Register #(.width(1)) register_13 (.D(in_2[12]), .en(in_1), .Q(out_3[12]), .clk(clock_1_out));  // open: clr
  Register #(.width(1)) register_14 (.D(in_2[13]), .en(in_1), .Q(out_3[13]), .clk(clock_1_out));  // open: clr
  Register #(.width(1)) register_15 (.D(in_2[14]), .en(in_1), .Q(out_3[14]), .clk(clock_1_out));  // open: clr
  Register #(.width(1)) register_16 (.D(in_2[15]), .en(in_1), .Q(out_3[15]), .clk(clock_1_out));  // open: clr
endmodule
