// Logisim project RAM16K.circ as structural Verilog: 1 circuit, main circuit main
module main (
  input  [15:0] Input,
  input  Load,
  input  [13:0] Address,
  output [15:0] Output
);

  wire clock_1_out, demultiplexer_1_out0, demultiplexer_1_out1, demultiplexer_1_out2, demultiplexer_1_out3;
  wire [15:0] ram_1_data, ram_2_data, ram_3_data, ram_4_data;

  Demultiplexer #(.select(2)) demultiplexer_1 (
    .out0(demultiplexer_1_out0), .out1(demultiplexer_1_out1), .out2(demultiplexer_1_out2),
    .out3(demultiplexer_1_out3), .in(Load), .sel(Address[13:12]));  // open: en
  RAM #(.addrWidth(12), .dataWidth(16), .bus("separate")) ram_1 (
    .addr(Address[11:0]), .din(Input), .data(ram_1_data), .str(demultiplexer_1_out0), .clk(clock_1_out));  // open: sel, ld, clr
  RAM #(.addrWidth(12), .dataWidth(16), .bus("separate")) ram_2 (
    .addr(Address[11:0]), .din(Input), .data(ram_2_data), .str(demultiplexer_1_out2), .clk(clock_1_out));  // open: sel, ld, clr
  Clock clock_1 (.out(clock_1_out));
  RAM #(.addrWidth(12), .dataWidth(16), .bus("separate")) ram_3 (
    .addr(Address[11:0]), .din(Input), .data(ram_3_data), .str(demultiplexer_1_out1), .clk(clock_1_out));  // open: sel, ld, clr
  RAM #(.addrWidth(12), .dataWidth(16), .bus("separate")) ram_4 (
    .addr(Address[11:0]), .din(Input), .data(ram_4_data), .str(demultiplexer_1_out3), .clk(clock_1_out));  // open: sel, ld, clr
  Multiplexer #(.select(2), .width(16)) multiplexer_1 (
    .in0(ram_1_data), .in1(ram_3_data), .in2(ram_2_data), .in3(ram_4_data), .out(Output), .sel(Address[13:12]));  // open: en

  // Notes on the sheet:
  //   RAM16K
endmodule
