// Logisim project Jumper.circ as structural Verilog: 1 circuit, main circuit main
module main (
  input  zr,
  input  ng,
  input  j1,
  input  j2,
  input  j3,
  output jump
);

  wire and_1_out, and_2_out, and_3_out, and_4_out, not_1_out, not_2_out, or_1_out;

  not not_1 (not_1_out, ng);
  not not_2 (not_2_out, zr);
  and and_1 (and_1_out, ng, j1);
  and and_2 (and_2_out, zr, j2);
  and and_3 (and_3_out, not_1_out, not_2_out);
  or or_1 (or_1_out, and_1_out, and_2_out);
  and and_4 (and_4_out, and_3_out, j3);
  or or_2 (jump, or_1_out, and_4_out);
endmodule
